// Logisim project BIN2DEC.circ as structural Verilog: 1 circuit, main circuit main
module main (
  input  [7:0] in_1,
  output [7:0] out_2
);

  wire and_1_out, and_2_out, and_3_out, and_9_out, and_10_out, and_11_out, and_12_out, and_13_out,
       and_14_out, and_15_out, and_16_out, and_17_out, and_18_out, and_19_out, and_20_out, and_21_out,
       and_22_out, and_23_out, and_24_out, and_25_out, and_26_out, and_27_out, and_28_out, and_29_out,
       and_30_out, and_31_out, and_32_out, not_1_out, not_2_out, not_3_out, not_4_out, not_5_out, not_6_out,
       not_7_out, not_8_out, not_9_out, or_1_out, or_2_out, or_3_out, or_5_out, or_6_out, or_7_out, or_8_out,
       or_9_out, or_10_out, or_11_out, or_12_out, xor_1_out, xor_2_out, xor_3_out, xor_4_out, xor_5_out,
       xor_6_out, xor_7_out, xor_8_out, xor_9_out, xor_10_out, xor_11_out, xor_12_out, xor_13_out,
       xor_14_out, xor_15_out, xor_16_out;
  wire [1:0] and_5_out;
  wire [7:0] and_6_out, and_7_out, and_8_out, or_4_out;
  wire [7:7] nor_1_out;

  or or_1 (or_1_out, in_1[2], in_1[3], in_1[4]);
  and and_1 (and_1_out, in_1[5], in_1[6]);
  or or_2 (or_2_out, in_1[3], in_1[4], in_1[5]);
  and and_2 (and_2_out, in_1[6], in_1[7]);
  and and_3 (and_3_out, or_1_out, and_1_out);
  and and_4 (and_5_out[1], or_2_out, and_2_out);
  or or_3 (or_3_out, and_3_out, in_1[7]);
  not not_1 (not_1_out, and_5_out[1]);
  and and_5 (and_5_out[0], or_3_out, not_1_out);
  nor nor_1 (nor_1_out[7], and_5_out[0], and_5_out[1]);
  assign and_6_out = {8{1'b0}} & {8{nor_1_out[7]}};  // AND_Gate and_6, 8 bits wide
  assign and_7_out = 8'h64 & {8{and_5_out[0]}};  // AND_Gate and_7, 8 bits wide
  assign and_8_out = 8'hc8 & {8{and_5_out[1]}};  // AND_Gate and_8, 8 bits wide
  assign or_4_out = and_6_out | and_7_out | and_8_out;  // OR_Gate or_4, 8 bits wide
  not not_2 (not_2_out, or_4_out[7]);
  not not_3 (not_3_out, or_4_out[4]);
  not not_4 (not_4_out, or_4_out[5]);
  not not_5 (not_5_out, or_4_out[6]);
  not not_6 (not_6_out, or_4_out[2]);
  not not_7 (not_7_out, or_4_out[3]);
  not not_8 (not_8_out, or_4_out[0]);
  not not_9 (not_9_out, or_4_out[1]);
  xor xor_1 (xor_1_out, 1'b1, not_8_out);
  and and_9 (and_9_out, 1'b1, not_8_out);
  xor xor_2 (xor_2_out, and_9_out, not_9_out);
  and and_10 (and_10_out, and_9_out, not_9_out);
  xor xor_3 (xor_3_out, and_10_out, not_6_out);
  and and_11 (and_11_out, and_10_out, not_6_out);
  xor xor_4 (xor_4_out, and_11_out, not_7_out);
  and and_12 (and_12_out, and_11_out, not_7_out);
  xor xor_5 (xor_5_out, and_12_out, not_3_out);
  and and_13 (and_13_out, and_12_out, not_3_out);
  xor xor_6 (xor_6_out, and_13_out, not_4_out);
  and and_14 (and_14_out, and_13_out, not_4_out);
  xor xor_7 (xor_7_out, and_14_out, not_5_out);
  and and_15 (and_15_out, and_14_out, not_5_out);
  xor xor_8 (xor_8_out, and_15_out, not_2_out);
  and and_16 (and_16_out, and_15_out, not_2_out);
  xor xor_9 (xor_9_out, xor_1_out, in_1[0]);
  and and_17 (and_17_out, xor_1_out, in_1[0]);
  xor xor_10 (xor_10_out, xor_2_out, in_1[1]);
  and and_18 (and_18_out, xor_2_out, in_1[1]);
  xor xor_11 (xor_11_out, xor_3_out, in_1[2]);
  and and_19 (and_19_out, xor_3_out, in_1[2]);
  xor xor_12 (xor_12_out, xor_4_out, in_1[3]);
  and and_20 (and_20_out, xor_4_out, in_1[3]);
  xor xor_13 (xor_13_out, xor_5_out, in_1[4]);
  and and_21 (and_21_out, xor_5_out, in_1[4]);
  xor xor_14 (xor_14_out, xor_6_out, in_1[5]);
  and and_22 (and_22_out, xor_6_out, in_1[5]);
  xor xor_15 (xor_15_out, xor_7_out, in_1[6]);
  and and_23 (and_23_out, xor_7_out, in_1[6]);
  xor xor_16 (xor_16_out, xor_8_out, in_1[7]);
  and and_24 (and_24_out, xor_8_out, in_1[7]);
  xor xor_17 (out_2[0], 1'b0, xor_9_out);
  and and_25 (and_25_out, 1'b0, xor_9_out);
  xor xor_18 (out_2[1], or_5_out, xor_10_out);
  and and_26 (and_26_out, or_5_out, xor_10_out);
  xor xor_19 (out_2[2], or_6_out, xor_11_out);
  and and_27 (and_27_out, or_6_out, xor_11_out);
  xor xor_20 (out_2[3], or_7_out, xor_12_out);
  and and_28 (and_28_out, or_7_out, xor_12_out);
  xor xor_21 (out_2[4], or_8_out, xor_13_out);
  and and_29 (and_29_out, or_8_out, xor_13_out);
  xor xor_22 (out_2[5], or_9_out, xor_14_out);
  and and_30 (and_30_out, or_9_out, xor_14_out);
  xor xor_23 (out_2[6], or_10_out, xor_15_out);
  and and_31 (and_31_out, or_10_out, xor_15_out);
  xor xor_24 (out_2[7], or_11_out, xor_16_out);
  and and_32 (and_32_out, or_11_out, xor_16_out);
  or or_5 (or_5_out, and_25_out, and_17_out);
  or or_6 (or_6_out, and_26_out, and_18_out);
  or or_7 (or_7_out, and_27_out, and_19_out);
  or or_8 (or_8_out, and_28_out, and_20_out);
  or or_9 (or_9_out, and_29_out, and_21_out);
  or or_10 (or_10_out, and_30_out, and_22_out);
  or or_11 (or_11_out, and_31_out, and_23_out);
  or or_12 (or_12_out, and_32_out, and_24_out);
endmodule
