// Logisim project rcd.circ as structural Verilog: 1 circuit, main circuit main
module main (
  input  [7:0] in_1,
  input  [7:0] in_2,
  input  [7:0] in_3,
  output [7:0] out_4,
  output [7:0] out_5,
  output [7:0] out_6
);

  wire button_1_out, clock_1_out, controlled_buffer_1_out, not_1_out, not_2_out;
  wire [3:0] main_1_p1, main_1_p2, main_1_p4, main_2_p1, main_2_p2, main_2_p4, main_3_p1, main_3_p2,
       main_3_p4, rom_1_data;
  wire [4:4] rom_1_data_2;
  wire [7:0] counter_1_q, main_1_p3, main_2_p3, main_3_p3, main_6_out_4, main_7_to_a, main_7_to_b,
       main_7_to_c, main_8_out_3, main_9_out_3, main_10_out_3, main_11_out_3, main_12_out_3, main_13_out_3,
       main_14_out_3, main_15_out_3, main_18_out_8, main_18_out_9, main_18_out_10, main_19_out_8,
       main_19_out_9, main_19_out_10, main_20_out_8, main_20_out_9, main_20_out_10, main_21_out_8,
       main_21_out_9, main_21_out_10, main_22_out_8, main_22_out_9, main_22_out_10, main_23_out_8,
       main_23_out_9, main_23_out_10, main_24_out_8, main_24_out_9, main_24_out_10, main_25_out_8,
       main_25_out_9, main_25_out_10, main_26_out_8, main_26_out_9, main_26_out_10, main_27_out_8,
       main_27_out_9, main_27_out_10;
  wire [9:0] rom_2_data;
  wire [14:0] main_4_out_2;
  wire [29:10] rom_2_data_2;

  Button button_1 (.out(button_1_out));
  Clock clock_1 (.out(clock_1_out));
  Hex_Digit_Display hex_digit_display_1 (.value(main_1_p2));  // open: dp
  Hex_Digit_Display hex_digit_display_2 (.value(main_1_p1));  // open: dp
  // BIN2DEC_main main_1: pin names not known; wires that end beside it: main_1_p1, main_1_p2, main_1_p3, main_1_p4
  not not_1 (not_1_out, main_4_out_2[9]);
  not not_2 (not_2_out, rom_1_data_2[4]);
  assign controlled_buffer_1_out = not_2_out ? clock_1_out : 1'bz;  // Controlled_Buffer controlled_buffer_1
  Hex_Digit_Display hex_digit_display_3 (.value(main_1_p4));  // open: dp
  Hex_Digit_Display hex_digit_display_4 (.value(main_2_p1));  // open: dp
  Counter counter_1 (
    .load(main_4_out_2[9]), .D(main_6_out_4), .count(not_1_out), .Q(counter_1_q),
    .clk(controlled_buffer_1_out), .clr(button_1_out));  // open: carry
  Hex_Digit_Display hex_digit_display_5 (.value(main_2_p4));  // open: dp
  Hex_Digit_Display hex_digit_display_6 (.value(main_2_p2));  // open: dp
  // BIN2DEC_main main_2: pin names not known; wires that end beside it: main_2_p1, main_2_p2, main_2_p3, main_2_p4
  Hex_Digit_Display hex_digit_display_7 (.value(main_3_p2));  // open: dp
  Hex_Digit_Display hex_digit_display_8 (.value(main_3_p1));  // open: dp
  // BIN2DEC_main main_3: pin names not known; wires that end beside it: main_3_p1, main_3_p2, main_3_p3, main_3_p4
  ROM #(.dataWidth(5)) rom_1 (.addr(counter_1_q), .data({rom_1_data_2[4], rom_1_data}));  // open: sel
  assign {out_6, out_5, out_4} = main_4_out_2[11] ? {main_1_p3, main_2_p3, main_3_p3} : 24'bz;  // Controlled_Buffer controlled_buffer_2
  Hex_Digit_Display hex_digit_display_9 (.value(main_3_p4));  // open: dp
  INSTRCTR_main main_4 (.in_1(rom_1_data), .out_2(main_4_out_2));
  ROM #(.dataWidth(30)) rom_2 (.addr(counter_1_q), .data({rom_2_data_2, rom_2_data}));  // open: sel
  RAM_main main_5 (
    .out_5(main_1_p3), .in_1(rom_2_data_2[29:20]), .in_2(controlled_buffer_1_out), .in_3(main_27_out_8),
    .in_4(button_1_out));
  STEP_SELEC_main main_6 (.in_2(main_1_p3), .in_3(main_2_p3), .out_4(main_6_out_4), .in_1(main_3_p3));
  VAL_TRNSFR_main main_7 (
    .Inp_A(main_1_p3), .Inp_C(main_3_p3), .Inp_B(main_2_p3), .To_B(main_7_to_b), .To_A(main_7_to_a),
    .To_C(main_7_to_c));
  SFTRGT_main main_8 (.in_1(main_1_p3), .in_2(main_2_p3), .out_3(main_8_out_3));
  SFTLFT_main main_9 (.in_1(main_1_p3), .in_2(main_2_p3), .out_3(main_9_out_3));
  XNOR_main main_10 (.in_1(main_1_p3), .in_2(main_2_p3), .out_3(main_10_out_3));
  XOR_main main_11 (.in_1(main_1_p3), .in_2(main_2_p3), .out_3(main_11_out_3));
  NOR_main main_12 (.in_1(main_1_p3), .in_2(main_2_p3), .out_3(main_12_out_3));
  NAND_main main_13 (.in_1(main_1_p3), .in_2(main_2_p3), .out_3(main_13_out_3));
  OR_main main_14 (.in_1(main_1_p3), .in_2(main_2_p3), .out_3(main_14_out_3));
  AND_main main_15 (.in_1(main_1_p3), .in_2(main_2_p3), .out_3(main_15_out_3));
  RAM_main main_16 (
    .out_5(main_2_p3), .in_1(rom_2_data_2[19:10]), .in_2(controlled_buffer_1_out), .in_3(main_27_out_9),
    .in_4(button_1_out));
  RAM_main main_17 (
    .out_5(main_3_p3), .in_1(rom_2_data), .in_2(controlled_buffer_1_out), .in_3(main_27_out_10),
    .in_4(button_1_out));
  INP_SEL_main main_18 (
    .in_1({8{1'b0}}), .in_2({8{1'b0}}), .in_3({8{1'b0}}), .in_4(main_4_out_2[10]), .out_8(main_18_out_8),
    .out_9(main_18_out_9), .out_10(main_18_out_10), .in_5(in_1), .in_6(in_2), .in_7(in_3));
  INP_SEL_main main_19 (
    .in_1(main_18_out_8), .in_2(main_18_out_9), .in_3(main_18_out_10), .in_4(main_4_out_2[8]),
    .out_8(main_19_out_8), .out_9(main_19_out_9), .out_10(main_19_out_10), .in_5(main_7_to_a),
    .in_6(main_7_to_b), .in_7(main_7_to_c));
  INP_SEL_main main_20 (
    .in_1(main_19_out_8), .in_2(main_19_out_9), .in_3(main_19_out_10), .in_4(main_4_out_2[7]),
    .out_8(main_20_out_8), .out_9(main_20_out_9), .out_10(main_20_out_10), .in_5({8{1'b0}}),
    .in_6({8{1'b0}}), .in_7(main_8_out_3));
  INP_SEL_main main_21 (
    .in_1(main_20_out_8), .in_2(main_20_out_9), .in_3(main_20_out_10), .in_4(main_4_out_2[6]),
    .out_8(main_21_out_8), .out_9(main_21_out_9), .out_10(main_21_out_10), .in_5({8{1'b0}}),
    .in_6({8{1'b0}}), .in_7(main_9_out_3));
  INP_SEL_main main_22 (
    .in_1(main_21_out_8), .in_2(main_21_out_9), .in_3(main_21_out_10), .in_4(main_4_out_2[5]),
    .out_8(main_22_out_8), .out_9(main_22_out_9), .out_10(main_22_out_10), .in_5({8{1'b0}}),
    .in_6({8{1'b0}}), .in_7(main_10_out_3));
  INP_SEL_main main_23 (
    .in_1(main_22_out_8), .in_2(main_22_out_9), .in_3(main_22_out_10), .in_4(main_4_out_2[4]),
    .out_8(main_23_out_8), .out_9(main_23_out_9), .out_10(main_23_out_10), .in_5({8{1'b0}}),
    .in_6({8{1'b0}}), .in_7(main_11_out_3));
  INP_SEL_main main_24 (
    .in_1(main_23_out_8), .in_2(main_23_out_9), .in_3(main_23_out_10), .in_4(main_4_out_2[3]),
    .out_8(main_24_out_8), .out_9(main_24_out_9), .out_10(main_24_out_10), .in_5({8{1'b0}}),
    .in_6({8{1'b0}}), .in_7(main_12_out_3));
  INP_SEL_main main_25 (
    .in_1(main_24_out_8), .in_2(main_24_out_9), .in_3(main_24_out_10), .in_4(main_4_out_2[2]),
    .out_8(main_25_out_8), .out_9(main_25_out_9), .out_10(main_25_out_10), .in_5({8{1'b0}}),
    .in_6({8{1'b0}}), .in_7(main_13_out_3));
  INP_SEL_main main_26 (
    .in_1(main_25_out_8), .in_2(main_25_out_9), .in_3(main_25_out_10), .in_4(main_4_out_2[1]),
    .out_8(main_26_out_8), .out_9(main_26_out_9), .out_10(main_26_out_10), .in_5({8{1'b0}}),
    .in_6({8{1'b0}}), .in_7(main_14_out_3));
  INP_SEL_main main_27 (
    .in_1(main_26_out_8), .in_2(main_26_out_9), .in_3(main_26_out_10), .in_4(main_4_out_2[0]),
    .out_8(main_27_out_8), .out_9(main_27_out_9), .out_10(main_27_out_10), .in_5({8{1'b0}}),
    .in_6({8{1'b0}}), .in_7(main_15_out_3));

  // Notes on the sheet:
  //   contents of rom_1 (hex, n*v repeats v):
  //   0 0 1 c
  //   contents of rom_2 (hex, n*v repeats v):
  //   6002ab 1bff 501406 5
endmodule
